// Logisim project Mikroprozessor_A_8_v0.1.circ as structural Verilog: 1 circuit, main circuit main
module main (
);

  wire button_1_out, clock_1_out, not_1_out, undriven_2;
  wire [7:0] adder_1_out, controlled_buffer_1_out, register_1_q, register_2_q, rom_2_data, subtractor_1_out;
  wire [8:0] counter_1_q_2, undriven;
  wire [8:1] counter_1_q;
  wire [15:8] rom_1_data;

  Button button_1 (.out(button_1_out));
  Clock clock_1 (.out(clock_1_out));
  Counter #(.width(9), .max('h1ff)) counter_1 (
    .clr(button_1_out), .clk(clock_1_out), .D(undriven), .Q({counter_1_q, counter_1_q_2[0]}));  // open: load, up, count, carry
  Register register_1 (.D(undriven[8:1]), .Q(register_1_q));  // open: en, clk, clr
  Register register_2 (.D(undriven[8:1]), .Q(register_2_q));  // open: en, clk, clr
  Adder adder_1 (.a(register_1_q), .b(register_2_q), .out(adder_1_out));  // open: cin, cout
  Subtractor subtractor_1 (.a(register_1_q), .b(register_2_q), .out(subtractor_1_out));  // open: bin, bout
  Register register_3 (.D(controlled_buffer_1_out), .Q(undriven[8:1]));  // open: en, clk, clr
  assign controlled_buffer_1_out = not_1_out ? adder_1_out : 8'bz;  // Controlled_Buffer controlled_buffer_1
  not not_1 (not_1_out, undriven_2);
  assign controlled_buffer_1_out = undriven_2 ? subtractor_1_out : 8'bz;  // Controlled_Buffer controlled_buffer_2
  ROM #(.dataWidth(16)) rom_1 (.addr(counter_1_q), .data({rom_1_data, counter_1_q_2[8:1]}));
  Register register_4 (.D(undriven[8:1]), .Q(undriven[8:1]));  // open: en, clk, clr
  Register register_5 (.D(undriven[8:1]), .Q(undriven[8:1]));  // open: en, clk, clr
  Register register_6 (.D(rom_1_data), .Q(undriven[8:1]));  // open: en, clk, clr
  RAM ram_1 (.addr(undriven[8:1]), .data(undriven[8:1]));  // open: we, oe, clk
  ROM #(.addrWidth(9)) rom_2 (.addr(counter_1_q_2), .data(rom_2_data));

  // Notes on the sheet:
  //   contents of rom_1 (hex, n*v repeats v):
  //   ff
endmodule
